# Fritzing sketch NumberMagic (saved by Fritzing 0.9.10b)
breadboards: 1

parts:
  Composant1 = Arduino Uno (Rev3)
  LCD1 = LCD screen
  Keypad4x1 = Keypad Membran 4x4
  U1 = POT [knob_status=50% power=0.5W package=alps_pot]
  U2 = MAX7219 [package=dil24]
  LED1 = 5641AS-1 [part_number=5641AS-1 package="DIP (Dual Inline) [THT]"]
  R1 = Resistor [tolerance=±5% resistance=4.7k power=0.25 package=THT]
  R2 = Resistor [tolerance=±5% resistance=22k power=0.25 package=THT]
  C1 = Electrolytic Capacitor [capacitance=10µF voltage=50V package="100 mil [THT, electrolytic]"]
  C2 = Ceramic Capacitor [capacitance=100nF voltage=35V package="100 mil [THT, multilayer]"]
  C3 = Ceramic Capacitor [capacitance=100nF package="100 mil [THT, multilayer]"]
  U3 = 74HC595 [package="DIP16 [THT]"]
  C4 = Ceramic Capacitor [capacitance=100nF voltage=35V package="100 mil [THT, multilayer]"]
  R3 = Resistor [tolerance=±5% power=0.25 resistance=220 package=THT]

nets:
  N1: Composant1.A0, U3.ST_CP
  N2: Composant1.A1, U2.LOAD
  N3: Composant1.D8, Keypad4x1.Pin2
  N4: Composant1.D9_PWM, Keypad4x1.Pin1
  N5: Composant1.D11_PWM/MOSI, U2.DIN, U3.DS
  N6: Composant1.D13/SCK, U2.CLK, U3.SH_CP
  N7: Composant1.D2, Keypad4x1.Pin8
  N8: Composant1.D3_PWM, Keypad4x1.Pin7
  N9: Composant1.D4, Keypad4x1.Pin6
  N10: Composant1.D5_PWM, Keypad4x1.Pin5
  N11: Composant1.D6_PWM, Keypad4x1.Pin4
  N12: Composant1.D7, Keypad4x1.Pin3
  VCC: Composant1.5V, LCD1.VDD, U1.A, U2.VCC, R2.Pin_0, C1.+, C2.1, C3.1, U3.MR, U3.VCC, C4.0, R3.Pin_0
  GND: Composant1.GND, LCD1.VSS, LCD1.R/W, LCD1.LED-, U1.E, U2.GND, U2.GND2, C1.-, C2.0, C3.0, U3.GND, U3.OE, C4.1
  N13: LCD1.V0, U1.S
  N14: LCD1.RS, U3.Q1
  N15: LCD1.E, U3.Q3
  N16: LCD1.DB4, U3.Q4
  N17: LCD1.DB5, U3.Q5
  N18: LCD1.DB6, U3.Q6
  N19: LCD1.DB7, U3.Q7
  N20: LCD1.LED+, R3.Pin_1
  N21: U2.DIG0, LED1.cat1
  N22: U2.DIG2, LED1.cat3
  N23: U2.DIG3, LED1.cat4
  N24: U2.DIG1, LED1.cat2
  N25: U2.SEGA, LED1.anA
  N26: U2.SEGF, LED1.anF
  N27: U2.SEGB, LED1.anB
  N28: U2.SEGG, LED1.anG
  N29: U2.ISET, R1.Pin_1
  N30: U2.SEGC, LED1.anC
  N31: U2.SEGE, LED1.anE
  N32: U2.SEGDP, LED1.anDP
  N33: U2.SEGD, LED1.anD
  N34: R1.Pin_0, R2.Pin_1

custom parts:
  Keypad Membran 4x4: Membrane Keypad 4x4 Matrix
  5641AS-1: 4 digit 7 segment common cathode LED display
